# Fritzing sketch Licenta (saved by Fritzing 1.0.4)

parts:
  VCC1 = Battery  # not connected
  Part1 = LCD1602-I2C
  Raspberry_Pi_1 = Raspberry Pi 3 [part_number=RPI-3-V1.2]
  U1 = TRANSCHIPTC5747 [package=camera_sfv24r-2st_2]  # not connected

nets:
  GND: Part1.GND, Raspberry_Pi_1.GND
  VCC: Part1.VCC, Raspberry_Pi_1.3v3
  N1: Part1.SDA, Raspberry_Pi_1.GPIO2
  N2: Part1.SCL, Raspberry_Pi_1.GPIO3

custom parts:
  Battery: Your standard 2x 18650 battery pack (7,4 Volts)
  LCD1602-I2C: A standard character display, usually with 2x16 characters. Comes in many colors with LCM1602 IIC attached.
